# Fritzing sketch Perfboard (saved by Fritzing 0.9.4)
perfboards: 1

parts:
  J1 = female pin header, 15 pins [form="♀ (female)"]
  J2 = female pin header, 15 pins [form="♀ (female)"]
  R1 = Resistor Mini [tolerance=±5% resistance=100 package=THT]
  R2 = Resistor Mini [tolerance=±5% resistance=100 package=THT]
  R3 = Resistor Mini [tolerance=±5% resistance=100 package=THT]
  R4 = Resistor Mini [tolerance=±5% resistance=100 package=THT]
  R5 = Resistor Mini [tolerance=±5% resistance=100 package=THT]
  R6 = Resistor Mini [tolerance=±5% resistance=100 package=THT]
  R7 = Resistor Mini [tolerance=±5% resistance=100 package=THT]
  J3 = female alternating pin header, 5 pins [form="♀ (female)"]
  J4 = female alternating pin header, 5 pins [form="♀ (female)"]
  R8 = Resistor [tolerance=±5% resistance=100 package="0805 [SMD]"]
  J6 = Camdenboss CTB0158-2 [part_number=CTB0158-2 package=THT]
  J7 = Camdenboss CTB0158-3 [part_number=CTB0158-3 package=THT]
  J8 = Camdenboss CTB0158-3 [part_number=CTB0158-3 package=THT]
  J9 = Camdenboss CTB0158-3 [part_number=CTB0158-3 package=THT]
  J10 = Camdenboss CTB0158-3 [part_number=CTB0158-3 package=THT]
  Q1 = MOSFET-NCHANNEL [package=to220v]
  R9 = Resistor Mini [tolerance=±5% resistance=100 package=THT]
  R10 = Resistor Mini [tolerance=±5% resistance=100k package=THT]
  J5 = Camdenboss CTB0158-5 [part_number=CTB0158-5 package=THT]
  SW1 = ENCODER_RGB_CA [package=encoder_led_3]
  U1 = SWITCH-SPST-2 [package=switch-spst-vertical]
  U2 = POT [package=pot_alpha_rv16af-20]
  U3 = POT [package=pot_alpha_rv16af-20]
  U4 = POT [package=pot_alpha_rv16af-20]
  U5 = POT [package=pot_alpha_rv16af-20]
  Part1 = ws2812b [package="smd 2812b"]
  Part2 = Arduino Nano (Rev3.0) (ICSP)
  7_Segment1 = 7 Segment Display

nets:
  N1: J1.pin1, J6.terminal_1, J6.terminal_2, U1.P, Part2.VIN
  N2: J1.pin2, J2.pin4, Part2.GND
  N3: J1.pin3, J2.pin3, Part2.RESET
  N4: J1.pin4, Part2.5V
  N5: J1.pin5, J7.terminal_3, J8.terminal_3, J10.terminal_3, U2.E, U3.E, U5.E, Part2.A7
  N6: J1.pin6, Part2.A6
  N7: J1.pin7, J8.terminal_2, U2.S, Part2.A5
  N8: J1.pin8, J7.terminal_2, U3.S, Part2.A4
  N9: J1.pin9, J9.terminal_2, U4.S, Part2.A3
  N10: J1.pin10, J10.terminal_2, U5.S, Part2.A2
  N11: J1.pin11, J5.terminal_3, SW1.A, Part2.A1
  N12: J1.pin12, Part1.DIN, Part2.A0
  N13: J1.pin13, Part2.AREF
  N14: J1.pin14, Part2.3V3
  N15: J1.pin15, R8.Pin_0, Part2.D13/SCK
  N16: J2.pin1, Part2.D1/TX
  N17: J2.pin2, Part2.D0/RX
  N18: J2.pin5, J5.terminal_2, SW1.+, Part2.D2
  N19: J2.pin6, Part2.D3
  N20: J2.pin7, R7.Pin_0, Part2.D4
  N21: J2.pin8, R9.Pin_0, Part2.D5
  N22: J2.pin9, R6.Pin_0, Part2.D6
  N23: J2.pin10, R5.Pin_0, Part2.D7
  N24: J2.pin11, R4.Pin_0, Part2.D8
  N25: J2.pin12, R3.Pin_0, Part2.D9
  N26: J2.pin13, J3.pin3, J4.pin3, Part2.D10, 7_Segment1.common_anode
  N27: J2.pin14, R2.Pin_0, Part2.D11/MOSI
  N28: J2.pin15, R1.Pin_0, Part2.D12/MISO
  N29: R1.Pin_1, J3.pin5, 7_Segment1.Segment_B
  N30: R2.Pin_1, J3.pin4, 7_Segment1.Segment_A
  N31: R3.Pin_1, J3.pin2, 7_Segment1.Segment_F
  N32: R4.Pin_1, J3.pin1, 7_Segment1.Segment_G
  N33: R5.Pin_1, J4.pin4, 7_Segment1.Segment_C
  N34: R6.Pin_1, J4.pin2, 7_Segment1.Segment_D
  N35: R7.Pin_1, J4.pin1, 7_Segment1.Segment_E
  N36: J4.pin5, R8.Pin_1, 7_Segment1.Segment_DP
  N37: J7.terminal_1, U3.A
  N38: J8.terminal_1, J9.terminal_1, J10.terminal_1, J5.terminal_4, SW1.B, U2.A, U4.A, U5.A
  N39: J9.terminal_3, U4.E
  N40: Q1.G, R9.Pin_1, R10.Pin_1
  N41: Q1.S, R10.Pin_0
  N42: J5.pin5, J5.terminal_5, SW1.C
  N43: J5.terminal_1, SW1.-B

notes:
  External 5V supply
  GND (Must be common with Arduino power supply)
  Red: +
  Black: GND
  Yellow: SW
  Green: DT
  Purple: CLK
  Main strip Vout
  5 - 12V supply
  GND (Must be common with the LED strip power supply)

custom parts:
  Resistor Mini: A generic resistor (0.25W)
